// Logisim project count_up_with_pause.circ as structural Verilog: 1 circuit, main circuit main
module main (
  input  SW,
  input  Clock,
  output Q1,
  output Q0
);

  wire decoder_1_out0, decoder_1_out2, decoder_1_out3, decoder_1_out4, decoder_1_out5, decoder_1_out7,
       or_1_out, or_2_out;

  Decoder #(.select(3), .enable("false")) decoder_1 (
    .out0(decoder_1_out0), .out2(decoder_1_out2), .out3(decoder_1_out3), .out4(decoder_1_out4),
    .out5(decoder_1_out5), .out7(decoder_1_out7), .sel({Q1, Q0, SW}));  // open: out1, out6
  or or_1 (or_1_out, decoder_1_out2, decoder_1_out4, decoder_1_out5, decoder_1_out7);
  or or_2 (or_2_out, decoder_1_out0, decoder_1_out3, decoder_1_out4, decoder_1_out7);
  D_Flip_Flop d_ff_1 (.clk(Clock), .D(or_1_out), .Q(Q1));  // open: Qn, preset, en, reset
  D_Flip_Flop d_ff_2 (.clk(Clock), .D(or_2_out), .Q(Q0));  // open: Qn, preset, en, reset
endmodule
