// Logisim project 3to8_decoder.circ as structural Verilog: 1 circuit, main circuit main
module main (
  input  A2,
  input  A1,
  input  A0,
  output Out0,
  output Out1,
  output Out2,
  output Out3,
  output Out4,
  output Out5,
  output Out6,
  output Out7
);

  and and_1 (Out0, ~A2, ~A1, ~A0);  // AND_Gate
  and and_2 (Out1, ~A2, ~A1, A0);  // AND_Gate
  and and_3 (Out2, ~A2, A1, ~A0);  // AND_Gate
  and and_4 (Out3, ~A2, A1, A0);  // AND_Gate
  and and_5 (Out4, A2, ~A1, ~A0);  // AND_Gate
  and and_6 (Out5, A2, ~A1, A0);  // AND_Gate
  and and_7 (Out6, A2, A1, ~A0);  // AND_Gate
  and and_8 (Out7, A2, A1, A0);
endmodule
